# Fritzing sketch RPiToArduino (saved by Fritzing 0.9.3b)
breadboards: 1

parts:
  Q1 = MOSFET-NCHANNEL [package=to-92]
  Q2 = MOSFET-NCHANNEL [package=to-92]
  Raspberry_Pi_1 = Raspberry Pi 3 [part_number=RPI-3-V1.2]
  Part1 = Arduino Uno (Rev3)
  R1 = Resistor [tolerance=±5% resistance=10k package=THT]
  R2 = Resistor [tolerance=±5% resistance=10k package=THT]
  R3 = Resistor [tolerance=±5% resistance=10k package=THT]
  R4 = Resistor [tolerance=±5% resistance=10k package=THT]

nets:
  N1: Q1.D, Raspberry_Pi_1.GPIO2, R1.Pin_0
  N2: Q1.S, Q2.S, Part1.3V3, R1.Pin_1, R2.Pin_1
  N3: Q1.G, Part1.A4/SDA, R3.Pin_0
  N4: Q2.D, Raspberry_Pi_1.GPIO3, R2.Pin_0
  N5: Q2.G, Part1.A5/SCL, R4.Pin_0
  GND: Raspberry_Pi_1.GND, Part1.GND
  N6: Part1.5V, R3.Pin_1, R4.Pin_1

notes:
  Level shifting with MOSFET
  RaspberryPi to Arduino I2C connection
